# Fritzing sketch breadboard_hookup (saved by Fritzing 1.0.3b)
breadboards: 1

parts:
  Part1 = Adafruit Feather M4 Express CAN
  Grove1 = Grove OLED 128x96
  U1 = SIP - 4 pins [chip_label=IC package="SIP (Single Inline) [THT]"]

nets:
  N1: Part1.SCK, Grove1.SCL
  N2: Part1.A3, U1.TX
  N3: Part1.A2, U1.RX
  GND: Part1.GND, Grove1.GND, U1.GND
  VCC: Part1.+3V3, Grove1.VCC, U1.VCC
  N4: Part1.D5, Grove1.SDA

custom parts:
  SIP - 4 pins: A SIP stand-in part for whatever you want. With 4 pins on a 300 mil single inline package (SIP) footprint.
